# Fritzing sketch Thermistor (saved by Fritzing 1.0.2b)
breadboards: 1

parts:
  Part1 = Arduino Uno (Rev3) - ICSP  # not connected
  U2 = LCD-16X2 [package=lcd-16x2_noholes]
  R1 = Temperature Sensor (Thermistor) [thermistor_type=NTC package=THT]
  Part2 = Adafruit Proto Shield R3 [part_number="Adafruit #2077"]
  R2 = Resistor [tolerance=±5% power=0.25W resistance=220 package=THT]
  U3 = POT [knob_status=50% power=0.5W package=pot_alpha_rv16af-20]
  R3 = Resistor [tolerance=±5% resistance=220 package="2010 [SMD]"]

nets:
  N1: U2.VSS, U2.R_W, U2.K, U3.E
  N2: U2.VDD, U3.A, R3.Pin_1
  N3: U2.VO, U3.S
  N4: U2.RS, Part2.D12
  N5: U2.E, Part2.D11
  N6: U2.DB4, Part2.D5
  N7: U2.DB5, Part2.D4
  N8: U2.DB6, Part2.D3
  N9: U2.DB7, Part2.D2
  N10: R1.pin_0, Part2.+5V
  N11: R1.pin_1, Part2.A4, R2.Pin_0
  N12: Part2.GND, R2.Pin_1

custom parts:
  Adafruit Proto Shield R3: This prototyping shield is the best out there (well, we think so, at least), and now is even better with Version R3 - updated for the most compatibility with just about all the Arduinos! It works with UNO, Mega, Leonardo, NG, Diecimila, Duemilanove, and compatible Arduinos. Yun's and Arduino Ethernets have a chunky Ethernet jack that gets in the way of stacking, you can use the stacking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
